# Fritzing sketch fall-larm (saved by Fritzing 1.0.6)
breadboards: 1

parts:
  A1 = ESP32 H2-DevKitM-1
  MAX30102 = MakerFocus MAX30102
  3-Axis_Accelerometer1 = 3-Axis Accelerometer Breakout - MMA8452Q
  Larmknapp = Pushbutton [package="[THT]"]
  resetknapp = Pushbutton [package="[THT]"]
  R2 = Temperature Sensor (Thermistor) [thermistor_type=NTC package=THT]
  R3 = Resistor [tolerance=±5% power=0.25W resistance=10k package=THT]

nets:
  VIN: A1.Pin_1, MAX30102.VIN, 3-Axis_Accelerometer1.3.3V, R2.pin_0
  N1: A1.Pin_5, resetknapp.Pin_3, resetknapp.Pin_4
  N2: A1.Pin_6, Larmknapp.Pin_2
  N3: A1.Pin_10, R2.pin_1, R3.Pin_0
  GND: A1.Pin_13, A1.Pin_15, A1.Pin_16, A1.Pin_19, A1.Pin_21, A1.Pin_30, MAX30102.GND, 3-Axis_Accelerometer1.GND, Larmknapp.Pin_3, Larmknapp.Pin_4, resetknapp.Pin_1, resetknapp.Pin_2, R3.Pin_1
  N4: A1.Pin_26, MAX30102.SCL, 3-Axis_Accelerometer1.SCL
  N5: A1.Pin_27, MAX30102.SDA, 3-Axis_Accelerometer1.SDA

custom parts:
  ESP32 H2-DevKitM-1: ESP32-H2-DevKitM-1 is an entry-level development board based on Bluetooth® Low Energy and IEEE 802.15.4 combo module ESP32-H2-MINI-1 or ESP32-H2-MINI-1U.
  MakerFocus MAX30102: Oximeter module using the MAX30102 chip. As usual, if you want the mounting holes in pcb, you need to drag a hole over the pad in silkscreen to actually drill the hole (by default they are not drilled)
